// Logisim project mux8_1.circ as structural Verilog
module main (
  input  in_1,
  input  in_2,
  input  in_3,
  input  in_4,
  input  in_5,
  input  in_6,
  input  in_7,
  input  in_8,
  input  in_9,
  input  in_10,
  input  in_11,
  input  in_12,
  input  [2:0] in_13,
  output out_14,
  output out_15,
  output out_16
);

  logic_test logic_test_1 (.a(in_1), .b(in_2), .c(in_3), .d(in_4), .out1(out_14), .out2(out_15));
  mux8_1 mux8_1_1 (
    .a(in_5), .b(in_6), .c(in_7), .d(in_8), .e(in_9), .f(in_10), .g(in_11), .h(in_12), .ch(in_13),
    .data_out(out_16));
endmodule

// VHDL entity logic_test, as the project stores it:
library ieee;
use ieee.std_logic_1164.all;

entity logic_test is
    port (
        a, b, c, d : in std_logic;
        out1       : out std_logic;
        out2       : out std_logic
    );
end entity logic_test;

architecture bhv of logic_test is
begin
    out1 <= a and b and c and d;
    out2 <= a or b or c or d;
end architecture bhv;

// VHDL entity mux8_1, as the project stores it:
library ieee;
use ieee.std_logic_1164.all;

entity mux8_1 is
    port (
        a, b, c, d, e, f, g, h : in std_logic;
        ch                   : in std_logic_vector(2 downto 0);
        data_out             : out std_logic
    );
end entity mux8_1;

architecture bhv of mux8_1 is
begin
    process(a, b, c, d, e, f, g, h, ch)
    begin
        case ch is
            when "000" => data_out <= a;
            when "001" => data_out <= b;
            when "010" => data_out <= c;
            when "011" => data_out <= d;
            when "100" => data_out <= e;
            when "101" => data_out <= f;
            when "110" => data_out <= g;
            when "111" => data_out <= h;
            when others => data_out <= '0';
        end case;
    end process;
end architecture bhv;
