// Logisim project segment.circ as structural Verilog
module main (
  input  [2:0] ch
);

  wire [7:0] seg7_letters_1_segments;

  seg7_letters seg7_letters_1 (.ch(ch), .segments(seg7_letters_1_segments));
  _7_Segment_Display u_7_segment_display_1 (
    .g(seg7_letters_1_segments[1]), .f(seg7_letters_1_segments[2]), .a(seg7_letters_1_segments[7]),
    .b(seg7_letters_1_segments[6]), .e(seg7_letters_1_segments[3]), .d(seg7_letters_1_segments[4]),
    .c(seg7_letters_1_segments[5]), .dp(seg7_letters_1_segments[0]));
endmodule

// VHDL entity logic_test, as the project stores it:
library ieee;
use ieee.std_logic_1164.all;

entity logic_test is
    port (
        a, b, c, d : in std_logic;
        out1       : out std_logic;
        out2       : out std_logic
    );
end entity logic_test;

architecture bhv of logic_test is
begin
    out1 <= a and b and c and d;
    out2 <= a or b or c or d;
end architecture bhv;

// VHDL entity mux8_1, as the project stores it:
library ieee;
use ieee.std_logic_1164.all;

entity mux8_1 is
    port (
        a, b, c, d, e, f, g, h : in std_logic;
        ch                   : in std_logic_vector(2 downto 0);
        data_out             : out std_logic
    );
end entity mux8_1;

architecture bhv of mux8_1 is
begin
    process(a, b, c, d, e, f, g, h, ch)
    begin
        case ch is
            when "000" => data_out <= a;
            when "001" => data_out <= b;
            when "010" => data_out <= c;
            when "011" => data_out <= d;
            when "100" => data_out <= e;
            when "101" => data_out <= f;
            when "110" => data_out <= g;
            when "111" => data_out <= h;
            when others => data_out <= '0';
        end case;
    end process;
end architecture bhv;

// VHDL entity seg7_letters, as the project stores it:
library ieee;
use ieee.std_logic_1164.all;

entity seg7_letters is
    port (
        ch       : in  std_logic_vector(2 downto 0);
        segments : out std_logic_vector(7 downto 0)
    );
end entity seg7_letters;

architecture bhv of seg7_letters is
begin
    process(ch)
    begin
        case ch is
            when "000" => segments <= "11111010"; -- a
            when "001" => segments <= "00111110"; -- b
            when "010" => segments <= "00011010"; -- c
            when "011" => segments <= "01111010"; -- d
            when "100" => segments <= "10001110"; -- f
            when "101" => segments <= "11110110"; -- g
            when others => segments <= "00000000";
        end case;
    end process;
end architecture bhv;
